# Fritzing sketch bmp_bp (saved by Fritzing 0.9.3b)
breadboards: 1

parts:
  M1 = STM32F103C8T6 blue mini board
  M2 = STM32F103C8T6 blue mini board

nets:
  N1: M1.A8, M1.B11
  N2: M1.3.3V, M1.VBAT, M1.3.3
  N3: M1.G, M1.GND, M1.connector45, M1.Boot0
  N4: M1.DIO, M2.B14
  N5: M1.CLK, M2.A5
  N6: M2.G, M2.GND, M2.connector45, M2.Boot0

notes:
  Black Magic Probe
  pb14: swdio
  pa5: swclk
  pa10: swo
  usb cable
  Blue Pill Target
  dio: swdio
  dclk: swclk
  pb3: swo
  *no usb cable*
